# Fritzing sketch Iot based Automation (saved by Fritzing 0.9.4)
breadboards: 1

parts:
  B1 = Bolt WiFi Module [package=dip]
  M1 = fc-51 [package=THT]
  J1 = Basic Servo
  J2 = Basic Servo
  T1 = LM35 Temperature Sensor [package="TO92 [THT]"]

nets:
  GND: B1.pin1, M1.pin2, J1.gnd, J2.gnd, T1.GND
  N1: B1.pin4, J2.pulse
  N2: B1.pin6, M1.pin1
  N3: B1.pin7, T1.Vout
  VCC: B1.pin11, M1.pin3, J1.vcc, J2.vcc, T1.+Vs

notes:
  Proximity Sensor connected to pin 0
  This Servo is connected to pin 3 which will act as a Door Open/Close Knob.
  This Servo is connected to pin 2 which will act as a Temperature Knob.
  LM35 Module connected to pin A0

custom parts:
  Bolt WiFi Module: Bolt IoT platform gives you the capability to control your devices and collect data from IoT devices safely and securely no matter where you are. Get actionable insights by deploying machine learning algorithms with just a few clicks to detect anomalies as well as predict sensor values.
